# Fritzing sketch MICRO-PROJECT (saved by Fritzing 0.9.3b)
breadboards: 1

parts:
  Part1 = Arduino Uno (Rev3)
  U1 = LCD-16X2 [package=lcd-16x2_noholes]
  R1 = Resistor [tolerance=±5% resistance=220 package=THT]
  R2 = Resistor [tolerance=±5% resistance=220 package=THT]
  R3 = Resistor [tolerance=±5% resistance=220 package=THT]
  R4 = Resistor [tolerance=±5% resistance=10k package=THT]
  R5 = Resistor [tolerance=±5% resistance=10k package=THT]
  S1 = Pushbutton [package="[THT]"]
  S2 = Pushbutton [package="[THT]"]
  J2 = Piezo Speaker
  LED1 = LED - 5mm [color="Red (633nm)" package="5 mm [THT]"]
  LED2 = LED - 5mm [color="Red (633nm)" package="5 mm [THT]"]
  hc-sr1 = hc-sr04
  hc-sr2 = hc-sr04
  U2 = POT [package=alps_pot]

nets:
  N1: Part1.A0, U1.RS
  N2: Part1.A1, U1.E
  N3: Part1.A2, U1.DB4
  N4: Part1.A3, U1.DB5
  N5: Part1.A4/SDA, U1.DB6
  N6: Part1.A5/SCL, U1.DB7
  N7: Part1.D8, R3.Pin_1
  N8: Part1.D9_PWM, R1.Pin_1
  N9: Part1.D10_PWM/SS, J2.pin1
  GND: Part1.GND, Part1.D2, Part1.D3_PWM, U1.VSS, U1.K, S1.Pin_1, S1.Pin_2, S2.Pin_1, S2.Pin_2, J2.pin2, hc-sr1.GND, hc-sr2.GND, U2.A
  N10: Part1.D4, hc-sr2.Echo
  N11: Part1.D5_PWM, hc-sr2.Trig
  N12: Part1.D6_PWM, hc-sr1.Echo
  N13: Part1.D7, hc-sr1.Trig
  VCC: Part1.5V, U1.VDD, R2.Pin_1, R4.Pin_0, R5.Pin_0, hc-sr1.VCC, hc-sr2.VCC, U2.E
  N14: U1.VO, U2.S
  N15: U1.A, R2.Pin_0
  N16: R1.Pin_0, LED2.anode
  N17: R3.Pin_0, LED1.anode
  N18: R4.Pin_1, S2.Pin_3, S2.Pin_4
  N19: R5.Pin_1, S1.Pin_3, S1.Pin_4

// code stored in the sketch: MICRO.ino
#include <LiquidCrystal.h>
LiquidCrystal lcd(A0, A1, A2, A3, A4, A5);

//for first Ultrasonic sensor
const int trigPin = 7;
const int echoPin = 6;

//for second Ultrasonic sensor
const int trigPin1 = 5;
const int echoPin1 = 4;

//for addition button
const int pushButton = 2;
int buttonRead = 0;

//for subtraction button
const int pushButton1 = 3;
int buttonRead1 = 0;

//for buzzer
const int buzzer = 10;

const int led = 9;
const int led1 = 8;
const int output = 11;




class RoomDisinfector{

  public:

    int incomingGuests(int count){
      int duration, distance;
      digitalWrite(trigPin, LOW);
      delayMicroseconds(2);

      digitalWrite(trigPin, HIGH);
      delayMicroseconds(10);
      digitalWrite(trigPin, LOW);

      duration = pulseIn(echoPin, HIGH);
      distance = (duration*0.034)/2;

      if(distance <= 12){
        count = count + 1;
        digitalWrite(led, HIGH);
        delay(500);
        digitalWrite(led, LOW);
      }
      return count;
    }

    int outgoingGuests(){
      int duration1, distance1;
      int val=0;
      digitalWrite(trigPin1, LOW);
      delayMicroseconds(2);

      digitalWrite(trigPin1, HIGH);
      delayMicroseconds(10);
      digitalWrite(trigPin1, LOW);

      duration1 = pulseIn(echoPin1, HIGH);
      distance1 = (duration1*0.034)/2;

      if(distance1 <= 12){
          val = val+1;
          digitalWrite(led1, HIGH);
          delay(500);
          digitalWrite(led1, LOW);
        }

      buttonRead = digitalRead(pushButton);
      buttonRead1 = digitalRead(pushButton1);

      if (buttonRead == HIGH){
       val = val + 1;
       digitalWrite(led1, HIGH);
       delay(500);
       digitalWrite(led1, LOW);
      }

      if(buttonRead1 == HIGH){
       val = val-1;
       digitalWrite(led1, HIGH);
       delay(500);
       digitalWrite(led1, LOW);
      }
      return val;
    }

    void alarm(){
      tone(buzzer, 450);
      delay(3000);
      noTone(buzzer);

    }

    void lcdDisplay(int passedVal, int passedVal1){
     Serial.print("Incoming: ");
     Serial.println(passedVal);

     Serial.print("Outgoing: ");
     Serial.println(passedVal1);

     lcd.setCursor(12, 0);
     lcd.print(passedVal);
     lcd.setCursor(10, 1);
     lcd.print(passedVal1);



     }




};




void setup() {
  pinMode(trigPin, OUTPUT);
  pinMode(echoPin, INPUT);
  pinMode(trigPin1, OUTPUT);
  pinMode(echoPin1, INPUT);
  pinMode(pushButton, INPUT);
  pinMode(pushButton1, INPUT);
  pinMode(buzzer, OUTPUT);
  pinMode(led, OUTPUT);
  pinMode(led1, OUTPUT);

  Serial.begin(9600);
  lcd.begin(16, 2);
  lcd.setCursor(0, 0);
  lcd.print("Population: ");
  lcd.setCursor(0, 1);
  lcd.print("Outgoing: ");
}

void loop() {
  int count = 0;
  RoomDisinfector r;

  int temp, temp1;
  temp = r.incomingGuests(count);
  temp1 = r.outgoingGuests();

  r.lcdDisplay(temp, temp1);

  if(temp <= temp1){
    r.alarm();
    delay(300000);
    digitalWrite(output, HIGH);
  }
}
